# Fritzing sketch wristband_duallayer_pcb (saved by Fritzing 0.9.2b)
circuit board: 5.92597cm x 4.74755cm

parts:
  3_3_V_8_MHz = Arduino Pro Mini v13
  MPU_6050 = female pin header, 8 pins [form="♀ (female)"]
  Grove-GSR = Grove Buzz
  Part1 = NRF24L01+ Breakout Board
  J3 = male pin header, 2 pins [form="♂ (male)"]
  J4 = female pin header, 4 pins [form="♀ (female)"]

nets (from the pcb view):
  N1: 3_3_V_8_MHz.A4, MPU_6050.pin4
  N2: 3_3_V_8_MHz.A5, MPU_6050.pin3
  VCC: 3_3_V_8_MHz.RAW, MPU_6050.pin1, Grove-GSR.VCC, Part1.VCC, J3.pin1, J4.pin2
  GND: 3_3_V_8_MHz.GND, MPU_6050.pin2, Grove-GSR.GND, Part1.GND, J3.pin2, J4.pin1
  N3: 3_3_V_8_MHz.A2, Grove-GSR.SIG, J4.pin4
  N4: 3_3_V_8_MHz.D13/SCK, Part1.SCK
  N5: 3_3_V_8_MHz.D12/MISO, Part1.MISO
  N6: 3_3_V_8_MHz.D11_PWM/MOSI, Part1.MOSI
  N7: 3_3_V_8_MHz.D8, Part1.CS
  N8: 3_3_V_8_MHz.D7, Part1.CE

notes:
  VCC
  GND
  I2C Data
  I2C Clock
  Input Data
  Clock
  Output Data
  SPI Chip Select
  Activates TX or RX Mode

custom parts:
  NRF24L01+ Breakout Board: This breakout board is for the Nordic Semiconductor NRF24L01+ 2.4GHz RF transceiver IC.
